// Logisim project lab9.circ as structural Verilog: 2 circuits, main circuit main
module main (
  input  X,
  input  Y,
  input  Z,
  output S,
  output C
);

  wire and_1_out, and_2_out, xor_1_out;

  xor xor_1 (xor_1_out, X, Y);
  and and_1 (and_1_out, X, Y);
  xor xor_2 (S, xor_1_out, Z);
  and and_2 (and_2_out, xor_1_out, Z);
  or or_1 (C, and_2_out, and_1_out);
endmodule

module full_adder (
  input  [3:0] X,
  input  [3:0] Y,
  input  in_3,
  output [4:0] S
);

  wire main_1_c, main_2_c, main_3_c;

  main main_1 (.X(X[0]), .Y(Y[0]), .Z(in_3), .S(S[0]), .C(main_1_c));
  main main_2 (.X(X[1]), .Y(Y[1]), .Z(main_1_c), .S(S[1]), .C(main_2_c));
  main main_3 (.X(X[2]), .Y(Y[2]), .Z(main_2_c), .S(S[2]), .C(main_3_c));
  main main_4 (.X(X[3]), .Y(Y[3]), .Z(main_3_c), .S(S[3]), .C(S[4]));
endmodule
